# Fritzing sketch AutoPlantSketch (saved by Fritzing 0.9.3b)
breadboards: 1

parts:
  Part1 = Arduino Uno (Rev3)
  LCD1 = LCD screen  # not connected
  Part2 = Real Time Clock Module - DS1307 RTC Breakout Board
  Part3 = LED Tactile Button Breakout v10 [part_number=BOB-10467]
  U1 = POT [package=alps_pot]

nets:
  N1: Part1.D8, Part2.SDA
  N2: Part1.D3_PWM, Part3.3
  N3: Part1.D4, Part3.4
  N4: Part1.D5_PWM, U1.A
  N5: Part1.D6_PWM, Part2.SCL
  N6: Part1.D7, Part2.SQW
  5V: Part1.5V, Part2.5V, Part3.2, U1.S
  GND: Part1.GND, Part2.GND, Part3.1, U1.E
